# Fritzing sketch Schema (saved by Fritzing 0.9.4)
breadboards: 1

parts:
  Компонент1 = Arduino Uno (Rev3)
  S1 = Pushbutton [package="[THT]"]
  R2 = Resistor [tolerance=±5% resistance=220 package=THT]
  LED1 = LED - 5mm [color="Red (633nm)" package="5 mm [THT]"]

nets:
  N1: Компонент1.GND, S1.Pin_3, S1.Pin_4, LED1.cathode
  N2: Компонент1.D2, S1.Pin_1, S1.Pin_2
  N3: Компонент1.D7, R2.Pin_1
  N4: R2.Pin_0, LED1.anode
