# Fritzing sketch Schema (saved by Fritzing 0.9.4)
breadboards: 1

parts:
  Компонент1 = Arduino Uno (Rev3)
  R1 = Resistor [tolerance=±5% resistance=220 package=THT]
  S1 = Pushbutton [package="[THT]"]

nets:
  N1: Компонент1.GND, S1.Pin_1, S1.Pin_2
  N2: Компонент1.D2, R1.Pin_0, S1.Pin_3, S1.Pin_4
  N3: Компонент1.5V, R1.Pin_1
