# Fritzing sketch Schema (saved by Fritzing 0.9.4)
breadboards: 1

parts:
  Компонент1 = Arduino Uno (Rev3)
  R2 = Resistor [tolerance=±5% resistance=150 package=THT]
  LED2 = RGB LED (com. cathode, rgb) [package="5 mm [THT]"]
  R3 = Resistor [tolerance=±5% resistance=150 package=THT]
  R4 = Resistor [tolerance=±5% resistance=220 package=THT]

nets:
  N1: Компонент1.D9_PWM, R4.Pin_1
  N2: Компонент1.D10_PWM/SS, R3.Pin_1
  N3: Компонент1.D11_PWM/MOSI, R2.Pin_1
  N4: R2.Pin_0, LED2.blue_anode
  N5: LED2.red_anode, R4.Pin_0
  N6: LED2.green_anode, R3.Pin_0
