# Fritzing sketch Schema (saved by Fritzing 0.9.4)
breadboards: 1

parts:
  Компонент1 = Arduino Uno (Rev3)
  R5 = Trimmer Potentiometer [maximum_resistance=10kΩ package=THT]

nets:
  N1: Компонент1.A0, R5.wiper
  N2: Компонент1.5V, R5.leg2
  N3: Компонент1.GND, R5.leg1
