# Fritzing sketch Schema (saved by Fritzing 0.9.4)
breadboards: 1

parts:
  Компонент1 = Arduino Uno (Rev3)
  T1 = TMP36 Temperature Sensor [package="TO92 [THT]"]

nets:
  N1: Компонент1.A0, T1.Vout
  N2: Компонент1.5V, T1.+Vs
  GND: Компонент1.GND, T1.GND
